// Logisim project Project210.01.circ as structural Verilog: 1 circuit, main circuit main
module main (
);

  wire button_1_out, clock_1_out, d_ff_1_q, d_ff_1_qn, d_ff_2_q, d_ff_2_qn, d_ff_3_q, d_ff_3_qn, d_ff_4_q,
       d_ff_4_qn, not_1_out, not_2_out, not_3_out, not_4_out;

  Clock clock_1 (.out(clock_1_out));
  Button button_1 (.out(button_1_out));
  not not_1 (not_1_out, d_ff_4_q);
  LED led_1 (.in(not_1_out));
  D_Flip_Flop d_ff_1 (
    .clk(clock_1_out), .D(d_ff_1_qn), .Q(d_ff_1_q), .Qn(d_ff_1_qn), .preset(button_1_out));  // open: en, reset
  not not_2 (not_2_out, d_ff_3_q);
  LED led_2 (.in(not_2_out));
  D_Flip_Flop d_ff_2 (
    .clk(d_ff_1_q), .D(d_ff_2_qn), .Q(d_ff_2_q), .Qn(d_ff_2_qn), .preset(button_1_out));  // open: en, reset
  not not_3 (not_3_out, d_ff_2_q);
  LED led_3 (.in(not_3_out));
  D_Flip_Flop d_ff_3 (
    .clk(d_ff_2_q), .D(d_ff_3_qn), .Q(d_ff_3_q), .Qn(d_ff_3_qn), .preset(button_1_out));  // open: en, reset
  not not_4 (not_4_out, d_ff_1_q);
  LED led_4 (.in(not_4_out));
  D_Flip_Flop d_ff_4 (
    .clk(d_ff_3_q), .D(d_ff_4_qn), .Q(d_ff_4_q), .Qn(d_ff_4_qn), .preset(button_1_out));  // open: en, reset

  // Notes on the sheet:
  //   reset
  //   8
  //   LED3
  //   Q
  //   4
  //   LED2
  //   Q1
  //   2
  //   LED1
  //   Q2
  //   1
  //   LED
  //   Q3
endmodule
